# Fritzing sketch ProjectFInal (saved by Fritzing 0.9.3b)
breadboards: 1

parts:
  Part1 = Arduino Leonardo (Rev3b)
  HC-SR04_Sensor_1 = HC-SR04 Ultrasonic Distance Sensor
  HC-SR04_Sensor_2 = HC-SR04 Ultrasonic Distance Sensor
  R1 = Resistor [tolerance=±5% resistance=220 package=THT]
  R2 = Resistor [tolerance=±5% resistance=220 package=THT]
  R3 = Resistor [tolerance=±5% resistance=220 package=THT]
  R4 = Resistor [tolerance=±5% resistance=220 package=THT]

nets:
  N1: Part1.D5_PWM, HC-SR04_Sensor_2.TRIG
  N2: Part1.D6_PWM/A7, R3.Pin_1, R4.Pin_0
  VCC: Part1.5V, HC-SR04_Sensor_1.VCC, HC-SR04_Sensor_2.VCC
  GND: Part1.GND, HC-SR04_Sensor_1.GND, HC-SR04_Sensor_2.GND, R2.Pin_0, R4.Pin_1
  N3: Part1.D9_PWM/A9, HC-SR04_Sensor_1.TRIG
  N4: Part1.D10_PWM/A10, R1.Pin_1, R2.Pin_1
  N5: HC-SR04_Sensor_1.ECHO, R1.Pin_0
  N6: HC-SR04_Sensor_2.ECHO, R3.Pin_0

notes:
  2K
  1K
  Connected to computer via Micro USB
